// Logisim project custom_cpu.circ as structural Verilog: 4 circuits, main circuit full_computer
module main_cpu (
  input  clock_signal,
  input  halt,
  input  [7:0] RAM_out,
  input  reset,
  input  port_flag1,
  input  port_flag2,
  input  port_flag3,
  input  port_flag4,
  input  port_flag5,
  input  [7:0] port_in,
  input  port_in_store,
  output [7:0] RAM_in,
  output [15:0] RAM_address,
  output RAM_write,
  output RAM_output,
  output [7:0] port_out,
  output [7:0] port_address,
  output port_ack1,
  output port_ack2
);

  wire and_1_out, and_2_out, and_3_out, and_4_out, bitselector_1_out, not_1_out, not_2_out, or_1_out,
       or_2_out, or_3_out, program_counter_low_carry;
  wire [1:0] alu_1_cb;
  wire [2:0] flag_bitsel_register_q;
  wire [7:0] address_buffer_a_q, address_buffer_b_q, bus_register_2_register_value,
       bus_register_3_register_value, controlled_buffer_8_out, flag_register_q, program_counter_high_q,
       program_counter_low_q, register_1_q, register_2_q;
  wire [11:0] counter_1_q;
  wire [45:0] rom_1_data;

  Counter #(.max('hf), .width(4)) counter_1 (
    .clr(reset), .load(rom_1_data[31]), .clk(not_1_out), .D(4'b0000), .Q(counter_1_q[3:0]));  // open: up, count, carry
  not not_1 (not_1_out, and_1_out);
  ROM #(.addrWidth(12), .dataWidth(46)) rom_1 (
    .addr(counter_1_q),
    .data({rom_1_data[45:29], port_ack2, port_ack1, rom_1_data[26:10], RAM_output, RAM_write, rom_1_data[7:0]}));
  not not_2 (not_2_out, or_1_out);
  or or_1 (or_1_out, halt, rom_1_data[36]);
  and and_1 (and_1_out, clock_signal, not_2_out);
  Register register_1 (.D(RAM_in), .en(rom_1_data[25]), .clk(and_1_out), .Q(register_1_q), .clr(reset));
  and and_2 (and_2_out, bitselector_1_out, rom_1_data[20]);
  and and_3 (and_3_out, bitselector_1_out, rom_1_data[22]);
  assign RAM_in = rom_1_data[33] ? address_buffer_a_q : 8'bz;  // Controlled_Buffer controlled_buffer_1
  assign RAM_in = rom_1_data[35] ? address_buffer_b_q : 8'bz;  // Controlled_Buffer controlled_buffer_2
  assign RAM_in = rom_1_data[37] ? rom_1_data[45:38] : 8'bz;  // Controlled_Buffer controlled_buffer_3
  assign RAM_in = RAM_output ? RAM_out : 8'bz;  // Controlled_Buffer controlled_buffer_4
  Register RAM_high (.D(RAM_in), .en(rom_1_data[10]), .clk(and_1_out), .Q(RAM_address[15:8]), .clr(reset));
  Register RAM_low (.D(RAM_in), .en(rom_1_data[11]), .clk(and_1_out), .Q(RAM_address[7:0]), .clr(reset));
  assign RAM_in = rom_1_data[13] ? program_counter_high_q : 8'bz;  // Controlled_Buffer controlled_buffer_5
  Counter program_counter_high (
    .clr(reset), .load(or_2_out), .count(and_4_out), .clk(and_1_out), .D(RAM_in), .Q(program_counter_high_q));  // open: up, carry
  or or_2 (or_2_out, and_2_out, rom_1_data[19]);
  and and_4 (and_4_out, rom_1_data[30], program_counter_low_carry);
  assign RAM_in = rom_1_data[14] ? program_counter_low_q : 8'bz;  // Controlled_Buffer controlled_buffer_6
  Counter program_counter_low (
    .clr(reset), .load(or_3_out), .count(rom_1_data[30]), .clk(and_1_out), .D(RAM_in),
    .carry(program_counter_low_carry), .Q(program_counter_low_q));  // open: up
  or or_3 (or_3_out, and_3_out, rom_1_data[21]);
  assign RAM_in = rom_1_data[23] ? register_2_q : 8'bz;  // Controlled_Buffer controlled_buffer_7
  assign controlled_buffer_8_out = rom_1_data[24] ? RAM_in : 8'bz;  // Controlled_Buffer controlled_buffer_8
  Register port_address_register (.D(RAM_in), .en(rom_1_data[26]), .clk(and_1_out), .Q(port_address), .clr(reset));
  Register address_buffer_a (.D(RAM_in), .en(rom_1_data[32]), .clk(and_1_out), .Q(address_buffer_a_q), .clr(reset));
  Register address_buffer_b (.D(RAM_in), .en(rom_1_data[34]), .clk(and_1_out), .Q(address_buffer_b_q), .clr(reset));
  Register flag_register (
    .D({port_flag5, port_flag4, port_flag3, port_flag2, port_flag1, bus_register_2_register_value[7], alu_1_cb}),
    .en(rom_1_data[12]), .clk(and_1_out), .Q(flag_register_q), .clr(reset));
  Register register_2 (.D(port_in), .en(port_in_store), .clk(and_1_out), .Q(register_2_q), .clr(reset));
  bus_register bus_register_1 (
    .bus_in(RAM_in), .enable(rom_1_data[0]), .load(rom_1_data[1]), .clock_signal(and_1_out), .reset(reset),
    .register_value(counter_1_q[11:4]), .bus_out(RAM_in));
  bus_register bus_register_2 (
    .bus_in(RAM_in), .enable(rom_1_data[2]), .load(rom_1_data[3]), .clock_signal(and_1_out), .reset(reset),
    .register_value(bus_register_2_register_value), .bus_out(RAM_in));
  bus_register bus_register_3 (
    .bus_in(RAM_in), .enable(rom_1_data[4]), .load(rom_1_data[5]), .clock_signal(and_1_out), .reset(reset),
    .register_value(bus_register_3_register_value), .bus_out(RAM_in));
  ALU alu_1 (
    .register_a(bus_register_2_register_value), .register_b(bus_register_3_register_value),
    .operator(rom_1_data[18:15]), .cb_in(register_1_q), .secondary_output(rom_1_data[6]),
    .enable(rom_1_data[7]), .cb(alu_1_cb[0]), .bus_out(RAM_in));
  Hex_Digit_Display hex_digit_display_1 (.value(RAM_address[15:12]));  // open: dp
  Hex_Digit_Display hex_digit_display_2 (.value(RAM_address[11:8]));  // open: dp
  BitSelector bitselector_1 (.in(flag_register_q), .out(bitselector_1_out), .sel(flag_bitsel_register_q));
  Register #(.width(3)) flag_bitsel_register (
    .D(RAM_in[2:0]), .en(rom_1_data[29]), .clk(and_1_out), .Q(flag_bitsel_register_q), .clr(reset));
  Register register_3 (.D(controlled_buffer_8_out), .en(rom_1_data[24]), .clk(and_1_out), .Q(port_out), .clr(reset));
  LedBar ledbar_1 (
    .led0(counter_1_q[11]), .led1(counter_1_q[10]), .led2(counter_1_q[9]), .led3(counter_1_q[8]),
    .led4(counter_1_q[7]), .led5(counter_1_q[6]), .led6(counter_1_q[5]), .led7(counter_1_q[4]));
  Comparator comparator_1 (.a(bus_register_2_register_value), .b({8{1'b0}}), .eq(alu_1_cb[1]));  // open: gt, lt
  Hex_Digit_Display hex_digit_display_3 (.value(RAM_address[7:4]));  // open: dp
  Hex_Digit_Display hex_digit_display_4 (.value(RAM_address[3:0]));  // open: dp

  // Notes on the sheet:
  //   contents of rom_1 (hex, n*v repeats v):
  //   2400 40004800 80000202 13*0 2400 40004800 202 2400 4800 40000a00 2000000400 80000208 8*0 2400
  //   40004800 202 2400 40004800 220 2400 40004800 a00 410 0 80000208 4*0 2400 40004800 202 2400 40004800
  //   80000208 10*0 2400 40004800 202 2400 4800 40000a00 2000000400 220 80000088 7*0 2400 40004800 202
  //   2400 40004800 220 2400 40004800 a00 410 0 220 80000088 0 0 0 2400 40004800 202 2400 4800 40000a00
  //   2000000400 220 80008088 7*0 2400 40004800 202 2400 40004800 220 2400 40004800 a00 410 0 220 80008088
  //   0 0 0 2400 40004800 202 2400 4800 40000a00 2000000400 220 80010088 7*0 2400 40004800 202 2400
  //   40004800 220 2400 40004800 a00 410 0 220 80010088 0 0 0 2400 40004800 202 2400 4800 40000a00
  //   2000000400 220 80018088 7*0 2400 40004800 202 2400 40004800 220 2400 40004800 a00 410 0 220 18088 0
  //   0 0 2400 40004800 202 1080000000 12*0 2400 40004800 202 2400 40004800 220 80000088 9*0 2400 40004800
  //   202 2400 40004800 220 80008088 9*0 2400 40004800 202 2400 40004800 220 80010088 9*0 2400 40004800
  //   202 2400 40004800 220 80018088 9*0 2400 40004800 202 81000004 12*0 2400 40004800 202 80800008 12*0
  //   2400 40004800 202 84000004 12*0 2400 40004800 202 281000000 12*0 2400 40004800 202 100800000 12*0
  //   2400 40004800 202 284000000 12*0 2400 40004800 202 881000000 12*0 2400 40004800 202 480800000 12*0
  //   2400 40004800 202 884000000 12*0 2400 40004800 202 88000000 12*0 2400 40004800 202 90000000 12*0
  //   2400 40004800 202 2400 40004800 81000200 10*0 2400 40004800 202 2400 40004800 84000200 10*0 2400
  //   40004800 202 2400 40004800 2000080000 80200200 9*0 2400 40004800 202 2400 40004800 220 2400 40004800
  //   80010 80200200 6*0 2400 40004800 202 200080000 880200000 11*0 2400 40004800 202 2400 40004800
  //   2000100000 80400200 9*0 2400 40004800 202 2400 40004800 220 2400 40004800 100010 80400200 6*0 2400
  //   40004800 202 200100000 800400000 11*0 2400 40004800 202 a0000004 12*0 2400 40004800 202 2a0000000
  //   12*0 2400 40004800 202 8a0000000 12*0 2400 40004800 202 2400 40004800 a0000200 10*0 2400 40004800
  //   202 2400 40004800 2020000000 2000100000 80400200 8*0 2400 40004800 202 2400 40004800 6020000000
  //   2000100000 80400200 8*0 2400 40004800 202 2400 40004800 a020000000 2000100000 80400200 8*0 2400
  //   40004800 202 2400 40004800 e020000000 2000100000 80400200 8*0 2400 40004800 202 2400 40004800
  //   12020000000 2000100000 80400200 8*0 2400 40004800 202 2400 40004800 16020000000 2000100000 80400200
  //   8*0 2400 40004800 202 2400 40004800 1a020000000 2000100000 80400200 8*0 2400 40004800 202 2400
  //   40004800 1c020000000 2000100000 80400200 8*0 2400 40004800 202 2400 40004800 220 2400 40004800
  //   2020000000 100010 80400200 5*0 2400 40004800 202 2400 40004800 220 2400 40004800 6020000000 100010
  //   80400200 5*0 2400 40004800 202 2400 40004800 220 2400 40004800 a020000000 100010 80400200 5*0 2400
  //   40004800 202 2400 40004800 220 2400 40004800 e020000000 100010 80400200 5*0 2400 40004800 202 2400
  //   40004800 220 2400 40004800 12020000000 100010 80400200 5*0 2400 40004800 202 2400 40004800 220 2400
  //   40004800 16020000000 100010 80400200 5*0 2400 40004800 202 2400 40004800 220 2400 40004800
  //   1a020000000 100010 80400200 5*0 2400 40004800 202 2400 40004800 220 2400 40004800 1c020000000 100010
  //   80400200 5*0 2400 40004800 202 2020000000 200100000 880400000 10*0 2400 40004800 202 6020000000
  //   200100000 880400000 10*0 2400 40004800 202 a020000000 200100000 880400000 10*0 2400 40004800 202
  //   e020000000 200100000 880400000 10*0 2400 40004800 202 12020000000 200100000 880400000 10*0 2400
  //   40004800 202 16020000000 200100000 880400000 10*0 2400 40004800 202 1a020000000 200100000 880400000
  //   10*0 2400 40004800 202 1c020000000 200100000 880400000 10*0 2400 40004800 202 2400 4800 40000a00
  //   2000000400 180000200 8*0 2400 40004800 202 2400 40004800 220 2400 40004800 a00 410 180000200 5*0
  //   2400 40004800 202 2400 40004800 180000200 10*0 2400 40004800 202 2400 4800 40000a00 2000000400
  //   480000200 8*0 2400 40004800 202 2400 40004800 220 2400 40004800 a00 410 480000200 5*0 2400 40004800
  //   202 2400 40004800 480000200 10*0 2400 40004800 202 24 200000008 180000020 10*0 2400 40004800 202 24
  //   8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
  //   instruction register
  //   register a
  //   register b
  //   ALU
endmodule

module bus_register (
  input  [7:0] bus_in,
  input  enable,
  input  load,
  input  clock_signal,
  input  reset,
  output [7:0] register_value,
  output [7:0] bus_out
);

  wire not_1_out;
  wire [7:0] controlled_buffer_2_out;

  assign bus_out = enable ? register_value : 8'bz;  // Controlled_Buffer controlled_buffer_1
  assign controlled_buffer_2_out = not_1_out ? bus_in : 8'bz;  // Controlled_Buffer controlled_buffer_2
  not not_1 (not_1_out, enable);
  Register register_1 (.D(controlled_buffer_2_out), .en(load), .clk(clock_signal), .Q(register_value), .clr(reset));
endmodule

module ALU (
  input  [7:0] register_a,
  input  [7:0] register_b,
  input  [3:0] operator,
  input  [7:0] cb_in,
  input  secondary_output,
  input  enable,
  output cb,
  output [7:0] bus_out
);

  wire not_1_out;
  wire [2:0] bitfinder_1_index, bitfinder_2_index, bitfinder_3_index, bitfinder_4_index;
  wire [3:0] bitadder_1_out;
  wire [7:0] adder_1_cout, adder_1_out, bitfinder_1_found, bitfinder_2_found, bitfinder_3_found,
       bitfinder_4_found, comparator_1_gt, divider_1_out, divider_1_rem, multiplexer_1_out,
       multiplexer_2_out, multiplier_1_cout, multiplier_1_out, nand_1_out, negator_1_out,
       pull_resistor_1_node, shifter_1_out, shifter_2_out, shifter_3_out, subtractor_1_bout,
       subtractor_1_out, xor_1_out;
  wire [7:3] undriven_2, undriven_3, undriven_4, undriven_5;
  wire [7:4] undriven;

  or or_1 (cb, subtractor_1_bout[0], adder_1_cout[0]);
  Multiplexer #(.select(4), .width(8)) multiplexer_1 (
    .in0(adder_1_cout), .in1(subtractor_1_bout), .in2(multiplier_1_cout), .in3(divider_1_rem),
    .in12(bitfinder_1_found), .in13(bitfinder_2_found), .in14(bitfinder_3_found), .in15(bitfinder_4_found),
    .out(multiplexer_1_out), .sel(operator));  // open: in4, in5, in6, in7, in8, in9, in10, in11
  Adder adder_1 (.a(register_a), .b(register_b), .out(adder_1_out), .cin(cb_in[0]), .cout(adder_1_cout[0]));
  Subtractor subtractor_1 (
    .a(register_a), .b(register_b), .out(subtractor_1_out), .bin(cb_in[0]), .bout(subtractor_1_bout[0]));
  Multiplier multiplier_1 (
    .a(register_a), .b(register_b), .out(multiplier_1_out), .cin(cb_in), .cout(multiplier_1_cout));
  Divider divider_1 (.a(register_a), .b(register_b), .out(divider_1_out), .upper(cb_in), .rem(divider_1_rem));
  Negator negator_1 (.in(register_a), .out(negator_1_out));
  Comparator comparator_1 (
    .a(register_a), .b(register_b), .gt(comparator_1_gt[0]), .eq(comparator_1_gt[1]), .lt(comparator_1_gt[2]));
  assign nand_1_out = ~(register_a & register_b);  // NAND_Gate nand_1, 8 bits wide
  assign xor_1_out = register_a ^ register_b;  // XOR_Gate xor_1, 8 bits wide
  Shifter #(.shift("lr")) shifter_1 (.in(register_a), .\dist (register_b[2:0]), .out(shifter_1_out));
  Shifter #(.shift("ar")) shifter_2 (.in(register_a), .\dist (register_b[2:0]), .out(shifter_2_out));
  Shifter #(.shift("rr")) shifter_3 (.in(register_a), .\dist (register_b[2:0]), .out(shifter_3_out));
  BitAdder bitadder_1 (.in0(register_a), .out(bitadder_1_out));
  BitFinder bitfinder_1 (.in(register_a), .index(bitfinder_1_index), .found(bitfinder_1_found[0]));
  BitFinder #(.\type ("high1")) bitfinder_2 (.in(register_a), .index(bitfinder_2_index), .found(bitfinder_2_found[0]));
  BitFinder #(.\type ("low0")) bitfinder_3 (.in(register_a), .index(bitfinder_3_index), .found(bitfinder_3_found[0]));
  BitFinder #(.\type ("high0")) bitfinder_4 (.in(register_a), .index(bitfinder_4_index), .found(bitfinder_4_found[0]));
  Multiplexer #(.select(4), .width(8)) multiplexer_2 (
    .in0(adder_1_out), .in1(subtractor_1_out), .in2(multiplier_1_out), .in3(divider_1_out),
    .in4(negator_1_out), .in5(comparator_1_gt), .in6(nand_1_out), .in7(xor_1_out), .in8(shifter_1_out),
    .in9(shifter_2_out), .in10(shifter_3_out), .in11({undriven, bitadder_1_out}),
    .in12({undriven_2, bitfinder_1_index}), .in13({undriven_3, bitfinder_2_index}),
    .in14({undriven_4, bitfinder_3_index}), .in15({undriven_5, bitfinder_4_index}), .out(multiplexer_2_out));  // open: sel
  not not_1 (not_1_out, secondary_output);
  Pull_Resistor pull_resistor_1 (.node(pull_resistor_1_node));
  assign bus_out = enable ? pull_resistor_1_node : 8'bz;  // Controlled_Buffer controlled_buffer_1
  Multiplexer #(.width(8)) multiplexer_3 (
    .in0(multiplexer_1_out), .in1(multiplexer_2_out), .out(pull_resistor_1_node), .sel(not_1_out));
endmodule

module full_computer (
);

  wire button_1_out, button_2_out, clock_1_out, comparator_1_eq, comparator_2_eq, controlled_buffer_4_out,
       controlled_buffer_5_out, controlled_buffer_6_out, main_cpu_1_port_ack1, main_cpu_1_port_ack2,
       main_cpu_1_ram_output, main_cpu_1_ram_write, pull_resistor_1_node, pull_resistor_2_node;
  wire [4:0] controlled_buffer_2_out, pull_resistor_3_node;
  wire [7:0] controlled_buffer_1_out, controlled_buffer_3_out, main_cpu_1_port_address, main_cpu_1_port_out,
       main_cpu_1_ram_in, pull_resistor_4_node, ram_1_dout;
  wire [15:0] main_cpu_1_ram_address;

  Button button_1 (.out(button_1_out));
  Clock clock_1 (.out(clock_1_out));
  Button button_2 (.out(button_2_out));
  RAM #(.addrWidth(16), .trigger("high")) ram_1 (
    .addr(main_cpu_1_ram_address), .we(main_cpu_1_ram_write), .oe(main_cpu_1_ram_output),
    .din(main_cpu_1_ram_in), .dout(ram_1_dout));
  main_cpu main_cpu_1 (
    .clock_signal(clock_1_out), .halt(button_1_out), .RAM_out(ram_1_dout), .reset(button_2_out),
    .port_flag1(controlled_buffer_2_out[0]), .port_flag2(controlled_buffer_2_out[1]),
    .port_flag3(controlled_buffer_2_out[2]), .port_flag4(controlled_buffer_2_out[3]),
    .port_flag5(controlled_buffer_2_out[4]), .port_in(controlled_buffer_3_out),
    .port_in_store(controlled_buffer_4_out), .RAM_in(main_cpu_1_ram_in),
    .RAM_address(main_cpu_1_ram_address), .RAM_write(main_cpu_1_ram_write),
    .RAM_output(main_cpu_1_ram_output), .port_out(main_cpu_1_port_out),
    .port_address(main_cpu_1_port_address), .port_ack1(main_cpu_1_port_ack1), .port_ack2(main_cpu_1_port_ack2));
  assign controlled_buffer_1_out = comparator_1_eq ? main_cpu_1_port_out : 8'bz;  // Controlled_Buffer controlled_buffer_1
  assign controlled_buffer_2_out = comparator_2_eq ? pull_resistor_3_node : 5'bz;  // Controlled_Buffer controlled_buffer_2
  assign controlled_buffer_3_out = comparator_2_eq ? pull_resistor_4_node : 8'bz;  // Controlled_Buffer controlled_buffer_3
  assign controlled_buffer_4_out = comparator_2_eq ? controlled_buffer_5_out : 1'bz;  // Controlled_Buffer controlled_buffer_4
  assign controlled_buffer_5_out = comparator_2_eq ? main_cpu_1_port_ack1 : 1'bz;  // Controlled_Buffer controlled_buffer_5
  assign controlled_buffer_6_out = comparator_2_eq ? main_cpu_1_port_ack2 : 1'bz;  // Controlled_Buffer controlled_buffer_6
  Comparator comparator_1 (.a(main_cpu_1_port_address), .b(8'h2), .eq(comparator_1_eq));  // open: gt, lt
  Pull_Resistor pull_resistor_1 (.node(pull_resistor_1_node));
  assign pull_resistor_1_node = comparator_1_eq ? main_cpu_1_port_ack1 : 1'bz;  // Controlled_Buffer controlled_buffer_7
  Pull_Resistor pull_resistor_2 (.node(pull_resistor_2_node));
  assign pull_resistor_2_node = comparator_1_eq ? main_cpu_1_port_ack2 : 1'bz;  // Controlled_Buffer controlled_buffer_8
  Pull_Resistor pull_resistor_3 (.node(pull_resistor_3_node));
  Pull_Resistor pull_resistor_4 (.node(pull_resistor_4_node));
  Comparator comparator_2 (.a(main_cpu_1_port_address), .b(8'h1), .eq(comparator_2_eq));  // open: gt, lt
  Pull_Resistor pull_resistor_5 (.node(controlled_buffer_5_out));
  Pull_Resistor pull_resistor_6 (.node(controlled_buffer_6_out));
  TTY tty_1 (
    .data(controlled_buffer_1_out[6:0]), .clk(clock_1_out), .we(pull_resistor_1_node),
    .clr(pull_resistor_2_node));
  Keyboard keyboard_1 (
    .clk(clock_1_out), .re(controlled_buffer_5_out), .clr(controlled_buffer_6_out),
    .avail(pull_resistor_3_node[0]), .data(pull_resistor_4_node[6:0]));
endmodule
